// Logisim project pk16.circ as structural Verilog: 3 circuits, main circuit main
module main (
);

  wire [4:0] instruction_unit_1_clock_stage;
  wire [15:0] instruction_unit_1_instruction;

  instruction_unit instruction_unit_1 (
    .instruction(instruction_unit_1_instruction), .clock_stage(instruction_unit_1_clock_stage));  // open: memory_read, clock, load_instruction_pointer, input_instruction_pointer, instruction_pointer
  opcode_decoder opcode_decoder_1 (.opcode(instruction_unit_1_instruction));  // open: immediate_enable, operation_select, destination_register, source_register, immediate_value
endmodule

module instruction_unit (
  input  [7:0] memory_read,
  input  clock,
  input  load_instruction_pointer,
  input  [15:0] input_instruction_pointer,
  output [15:0] instruction,
  output [4:0] clock_stage,
  output [15:0] instruction_pointer
);

  wire counter_1_carry, decoder_1_out0, decoder_1_out1, decoder_1_out7;
  wire [2:0] counter_1_q;

  Counter #(.max('h7), .width(3)) counter_1 (
    .load(1'b0), .up(1'b1), .clk(clock), .carry(counter_1_carry), .Q(counter_1_q));  // open: clr, count, D
  Counter #(.max('hffff), .width(16)) counter_2 (
    .load(load_instruction_pointer), .up(1'b1), .clk(decoder_1_out7), .D(input_instruction_pointer),
    .Q(instruction_pointer));  // open: clr, count, carry
  Decoder #(.select(3)) decoder_1 (
    .out0(decoder_1_out0), .out1(decoder_1_out1), .out2(clock_stage[0]), .out3(clock_stage[1]),
    .out4(clock_stage[2]), .out5(clock_stage[3]), .out6(clock_stage[4]), .out7(decoder_1_out7),
    .sel(counter_1_q), .en(1'b1));
  Register register_1 (.D(memory_read), .en(decoder_1_out0), .clk(1'b1), .Q(instruction[7:0]));  // open: clr
  Register register_2 (.D(memory_read), .en(decoder_1_out1), .clk(1'b1), .Q(instruction[15:8]));  // open: clr
endmodule

module opcode_decoder (
  input  [15:0] opcode,
  output immediate_enable,
  output [6:0] operation_select,
  output [3:0] destination_register,
  output [3:0] source_register,
  output [7:0] immediate_value
);

  wire [3:3] not_1_out;

  not not_1 (not_1_out[3], opcode[15]);
  assign operation_select[6:3] = {4{not_1_out[3]}} & opcode[14:11];  // AND_Gate and_1, 4 bits wide
  assign destination_register = opcode[15] ? opcode[14:11] : 4'bz;  // Controlled_Buffer controlled_buffer_1
  assign destination_register = not_1_out[3] ? opcode[3:0] : 4'bz;  // Controlled_Buffer controlled_buffer_2

  assign immediate_enable = opcode[15];
  assign immediate_value = opcode[7:0];
  assign operation_select[2:0] = opcode[10:8];
  assign source_register = opcode[7:4];
endmodule
